# Fritzing sketch sketch (saved by Fritzing 0.9.3b)
breadboards: 1

parts:
  OLED = adafruit [part_number="Adafruit #3527"]
  WeMos_D1_Mini1 = WeMos D1 Mini
  DHT11 = DHT11_Temperature_and_Humitidy_Sensor
  Switch = SWITCH-MOMENTARY-2 [package=tactile-pth]

nets (from the schematic view):
  N1: OLED.connector2, WeMos_D1_Mini1.D2
  N2: OLED.connector3, WeMos_D1_Mini1.5V, DHT11.connector1
  N3: OLED.connector4, WeMos_D1_Mini1.D1
  N4: OLED.connector5, WeMos_D1_Mini1.G, DHT11.connector4, Switch.2
  N5: WeMos_D1_Mini1.D3, Switch.1
  N6: WeMos_D1_Mini1.D5, DHT11.connector2
